# Fritzing sketch CircuitDiagram (saved by Fritzing 1.0.6)
breadboards: 4

parts:
  Pico_H1 = Raspberry Pi Pico H
  U1 = 74HC595 [package="DIP16 [THT]"]
  U2 = 74HC595 [package="DIP16 [THT]"]
  U3 = 74HC595 [package="DIP16 [THT]"]
  C1 = Ceramic Capacitor [capacitance="100 nF" voltage=35V package="0603 [SMD, multilayer]"]
  LED1 = smd LED [color="Red (633nm)" package="0603 [SMD]"]
  LED2 = smd LED [color="Red (633nm)" package="0603 [SMD]"]
  LED3 = smd LED [color="Red (633nm)" package="0603 [SMD]"]
  LED4 = smd LED [color="Red (633nm)" package="0603 [SMD]"]
  LED5 = smd LED [color="Red (633nm)" package="0603 [SMD]"]
  R1 = Resistor [tolerance=±5% resistance=220 package="2512 [SMD]"]
  R2 = Resistor [tolerance=±5% resistance=220 package="2512 [SMD]"]
  R3 = Resistor [tolerance=±5% resistance=220 package="2512 [SMD]"]
  R4 = Resistor [tolerance=±5% resistance=220 package="2512 [SMD]"]
  R5 = Resistor [tolerance=±5% resistance=220 package="2512 [SMD]"]
  C2 = Ceramic Capacitor [capacitance="100 nF" voltage=35V package="0603 [SMD, multilayer]"]
  LED6 = smd LED [color="Red (633nm)" package="0603 [SMD]"]
  LED7 = smd LED [color="Red (633nm)" package="0603 [SMD]"]
  LED8 = smd LED [color="Red (633nm)" package="0603 [SMD]"]
  LED9 = smd LED [color="Red (633nm)" package="0603 [SMD]"]
  LED10 = smd LED [color="Red (633nm)" package="0603 [SMD]"]
  LED11 = smd LED [color="Red (633nm)" package="0603 [SMD]"]
  R6 = Resistor [tolerance=±5% resistance=220 package="2512 [SMD]"]
  R7 = Resistor [tolerance=±5% resistance=220 package="2512 [SMD]"]
  R8 = Resistor [tolerance=±5% resistance=220 package="2512 [SMD]"]
  R9 = Resistor [tolerance=±5% resistance=220 package="2512 [SMD]"]
  R10 = Resistor [tolerance=±5% resistance=220 package="2512 [SMD]"]
  R11 = Resistor [tolerance=±5% resistance=220 package="2512 [SMD]"]
  LED12 = smd LED [color="Red (633nm)" package="0603 [SMD]"]
  LED13 = smd LED [color="Red (633nm)" package="0603 [SMD]"]
  LED14 = smd LED [color="Red (633nm)" package="0603 [SMD]"]
  LED15 = smd LED [color="Red (633nm)" package="0603 [SMD]"]
  LED16 = smd LED [color="Red (633nm)" package="0603 [SMD]"]
  LED17 = smd LED [color="Red (633nm)" package="0603 [SMD]"]
  R12 = Resistor [tolerance=±5% resistance=220 package="2512 [SMD]"]
  R13 = Resistor [tolerance=±5% resistance=220 package="2512 [SMD]"]
  R14 = Resistor [tolerance=±5% resistance=220 package="2512 [SMD]"]
  R15 = Resistor [tolerance=±5% resistance=220 package="2512 [SMD]"]
  R16 = Resistor [tolerance=±5% resistance=220 package="2512 [SMD]"]
  R17 = Resistor [tolerance=±5% resistance=220 package="2512 [SMD]"]
  C3 = Ceramic Capacitor [capacitance="100 nF" voltage=35V package="0603 [SMD, multilayer]"]

nets:
  GND: Pico_H1.GND, U1.GND, U1.OE, U2.GND, U2.OE, U3.GND, U3.OE, C1.1, R1.Pin_1, R2.Pin_1, R3.Pin_1, R4.Pin_1, R5.Pin_1, C2.1, R6.Pin_1, R7.Pin_1, R8.Pin_1, R9.Pin_1, R10.Pin_1, R11.Pin_1, R12.Pin_1, R13.Pin_1, R14.Pin_1, R15.Pin_1, R16.Pin_1, R17.Pin_1, C3.1
  VCC: Pico_H1.3V3, U1.MR, U1.VCC, U2.MR, U2.VCC, U3.MR, U3.VCC, C1.0, C2.0, C3.0
  N1: Pico_H1.GP16, U3.DS
  N2: Pico_H1.GP15, U1.SH_CP, U2.SH_CP, U3.SH_CP
  N3: Pico_H1.GP14, U1.ST_CP, U2.ST_CP, U3.ST_CP
  N4: U1.Q1, LED2.cathode
  N5: U1.Q2, LED3.cathode
  N6: U1.Q3, LED4.cathode
  N7: U1.Q4, LED5.cathode
  N8: U1.DS, U2.Q7'
  N9: U1.Q0, LED1.cathode
  N10: U2.Q1, LED7.cathode
  N11: U2.Q2, LED8.cathode
  N12: U2.Q3, LED9.cathode
  N13: U2.Q4, LED10.cathode
  N14: U2.Q5, LED11.cathode
  N15: U2.DS, U3.Q7'
  N16: U2.Q0, LED6.cathode
  N17: U3.Q1, LED13.cathode
  N18: U3.Q2, LED14.cathode
  N19: U3.Q3, LED15.cathode
  N20: U3.Q4, LED16.cathode
  N21: U3.Q5, LED17.cathode
  N22: U3.Q0, LED12.cathode
  N23: LED1.anode, R1.Pin_0
  N24: LED2.anode, R2.Pin_0
  N25: LED3.anode, R3.Pin_0
  N26: LED4.anode, R4.Pin_0
  N27: LED5.anode, R5.Pin_0
  N28: LED6.anode, R6.Pin_0
  N29: LED7.anode, R7.Pin_0
  N30: LED8.anode, R8.Pin_0
  N31: LED9.anode, R9.Pin_0
  N32: LED10.anode, R10.Pin_0
  N33: LED11.anode, R11.Pin_0
  N34: LED12.anode, R12.Pin_0
  N35: LED13.anode, R13.Pin_0
  N36: LED14.anode, R14.Pin_0
  N37: LED15.anode, R15.Pin_0
  N38: LED16.anode, R16.Pin_0
  N39: LED17.anode, R17.Pin_0

notes:
  Hours
  Minutes
  Seconds

custom parts:
  Raspberry Pi Pico H: Raspberry Pi Pico H. Based around the RP2040 microcontroller the Pico H is a low cost microcontroller device bringing Raspberry Pi quality, cost, and easy of use to the microcontroller space.
